# Fritzing sketch globe-trotter_hJQwkbcnEe (saved by Fritzing 0.9.3b)
circuit board: 8.46667cm x 5.64444cm
breadboards: 1

parts:
  R1 = Resistor [tolerance=±5% resistance=100k package=THT]
  R2 = Resistor [tolerance=±5% resistance=100k package=THT]
  C1 = Ceramic Capacitor [capacitance=0.1µF package="100 mil [THT, multilayer]"]
  C2 = Ceramic Capacitor [capacitance=0.1µF package="100 mil [THT, multilayer]"]
  RobotDyn_Rotary_Encoder = IC, SIP package, 4 pins [chip_label="Rotary encoder"]
  Part1 = Arduino Uno (Rev3)

nets:
  N1: R1.Pin_0, Part1.D10_PWM/SS
  N2: R1.Pin_1, R2.Pin_1, Part1.D11_PWM/MOSI
  N3: R2.Pin_0, Part1.D9_PWM
  N4: C1.0, C2.0, RobotDyn_Rotary_Encoder.pin2, Part1.GND
  N5: C1.1, RobotDyn_Rotary_Encoder.pin4, Part1.D12/MISO
  N6: C2.1, RobotDyn_Rotary_Encoder.pin3, Part1.D13/SCK
  N7: RobotDyn_Rotary_Encoder.pin1, Part1.5V

notes:
  country 1
  country 2
  send pin
  receive pin
